// Logisim project maybeProject.circ as structural Verilog
// 12
module main (
  input  Stopper
);

  wire cdm_8_mark5_1_p1, cdm_8_mark5_1_p2, cdm_8_mark5_1_p4, cdm_8_mark5_1_p5, cdm_8_mark5_1_p6,
       cdm_8_mark5_1_p7, clock_1_out, code, data, in_out, IO_sel, Jump, mem, nand_1_out, not_1_out,
       not_2_out, not_3_out, Ram, \time ;
  wire [3:0] delayer4_1_out_5, delayer4_1_out_5_2, delayer4_1_out_6, delayer4_1_out_6_2, IO_adrr;
  wire [7:0] cdm_8_mark5_1_p11, cdm_8_mark5_1_p12, IOdatl;
  wire [7:4] cdm_8_mark5_1_p10;
  wire [31:0] _1, _1_1, _2, _2_1, _3, _3_1, _4, _4_1, _5, _5_1, _6, _6_1, _7, _8, _9, _10, _11, _12, _13,
       _14, _15, _16, _17, _18, _19, _20, _21, _22, _23, _24, _25, _26, _27, _28, _29, _30, _31, _32,
       cactus_generator_1_out;

  jumper jumper_1 (.in_3(32'h8), .out_5(_1), .chooser(Jump), .Selector(_1_1), .Clock(\time ));
  jumper jumper_2 (.in_3(32'h4), .out_5(_2), .chooser(Jump), .Selector(_2_1), .Clock(\time ));
  jumper jumper_3 (.in_3(32'he), .out_5(_3), .chooser(Jump), .Selector(_3_1), .Clock(\time ));
  DotMatrix #(.matrixcols(32), .matrixrows(32)) dotmatrix_1 (
    .col0(_1), .col1(_2), .col2(_3), .col3(_4), .col4(_5), .col5(_6), .col6(_7), .col7(_8), .col8(_9),
    .col9(_10), .col10(_11), .col11(_12), .col12(_13), .col13(_14), .col14(_15), .col15(_16), .col16(_17),
    .col17(_18), .col18(_19), .col19(_20), .col20(_21), .col21(_22), .col22(_23), .col23(_24), .col24(_25),
    .col25(_26), .col26(_27), .col27(_28), .col28(_29), .col29(_30), .col30(_31), .col31(_32));
  jumper jumper_4 (.in_3(32'h7c), .out_5(_4), .chooser(Jump), .Selector(_4_1), .Clock(\time ));
  jumper jumper_5 (.in_3(32'h5e), .out_5(_5), .chooser(Jump), .Selector(_5_1), .Clock(\time ));
  jumper jumper_6 (.in_3(32'h68), .out_5(_6), .chooser(Jump), .Selector(_6_1), .Clock(\time ));
  cactus_generator cactus_generator_1 (.clock(\time ), .out(cactus_generator_1_out));
  mover mover_1 (
    .in_1(\time ), .in_2(cactus_generator_1_out), .out_3(_32), .out_4(_31), .out_5(_30), .out_6(_29),
    .out_7(_28), .out_8(_27), .out_9(_26), .out_10(_25), .out_11(_24), .out_12(_23), .out_13(_22),
    .out_14(_21), .out_15(_20), .out_16(_19), .out_17(_18), .out_18(_17), .out_19(_16), .out_20(_15),
    .out_21(_14), .out_22(_13), .out_23(_12), .out_24(_11), .out_25(_10), .out_26(_9), .out_27(_8),
    .out_28(_7), .out_29(_6_1), .out_30(_5_1), .out_31(_4_1), .out_32(_3_1), .out_33(_2_1), .out_34(_1_1));
  Hex_Digit_Display hex_digit_display_1 (.value(delayer4_1_out_6));  // open: dp
  Button Space (.out(Jump));
  Hex_Digit_Display hex_digit_display_2 (.value(delayer4_1_out_5_2));  // open: dp
  Hex_Digit_Display hex_digit_display_3 (.value(delayer4_1_out_6_2));  // open: dp
  Hex_Digit_Display hex_digit_display_4 (.value(delayer4_1_out_5));  // open: dp
  delayer4 delayer4_1 (
    .out_5({delayer4_1_out_5_2, delayer4_1_out_5}), .out_6({delayer4_1_out_6, delayer4_1_out_6_2}),
    .Data(IOdatl), .Selector(IO_sel), .Adress(IO_adrr), .In_Out(in_out));
  not not_1 (not_1_out, not_1_out);
  // Probe on cdm_8_mark5_1_p5
  // Probe on cdm_8_mark5_1_p4
  // Probe on cdm_8_mark5_1_p2
  // Probe on cdm_8_mark5_1_p1
  // Probe on cdm_8_mark5_1_p6
  // Probe on nothing
  // CdM_8_mark5 cdm_8_mark5_1: pin names not known; wires that end beside it: cdm_8_mark5_1_p1, cdm_8_mark5_1_p2, \time , cdm_8_mark5_1_p4, cdm_8_mark5_1_p5, cdm_8_mark5_1_p6, cdm_8_mark5_1_p7, mem, in_out, {cdm_8_mark5_1_p10, IO_adrr}, cdm_8_mark5_1_p11, cdm_8_mark5_1_p12
  Decoder #(.disabled(0)) decoder_1 (.out0(code), .out1(data), .sel(cdm_8_mark5_1_p7), .en(mem));
  assign IOdatl = not_2_out ? cdm_8_mark5_1_p11 : 8'bz;  // Controlled_Buffer controlled_buffer_1
  not not_2 (not_2_out, in_out);
  assign cdm_8_mark5_1_p12 = in_out ? IOdatl : 8'bz;  // Controlled_Buffer controlled_buffer_2
  // Probe on {cdm_8_mark5_1_p10, IO_adrr}
  RAM ram_1 (.addr({cdm_8_mark5_1_p10, IO_adrr}), .data(IOdatl), .sel(Ram), .clk(\time ), .ld(in_out));  // open: clr
  ROM rom_1 (.addr({cdm_8_mark5_1_p10, IO_adrr}), .data(IOdatl), .sel(code));
  and and_1 (IO_sel, not_3_out, \time , data);
  Clock clock_1 (.out(clock_1_out));
  Pull_Resistor pull_resistor_1 (.node(\time ));
  Transistor transistor_1 (.in(clock_1_out), .out(\time ), .gate(Stopper));
  not not_3 (not_3_out, nand_1_out);
  and and_2 (Ram, nand_1_out, data);
  nand nand_1 (nand_1_out, cdm_8_mark5_1_p10[4], cdm_8_mark5_1_p10[5], cdm_8_mark5_1_p10[6], cdm_8_mark5_1_p10[7]);
  Pull_Resistor pull_resistor_2 (.node(IO_adrr[0]));
  Pull_Resistor pull_resistor_3 (.node(IO_adrr[1]));
  Pull_Resistor pull_resistor_4 (.node(IO_adrr[2]));
  Pull_Resistor pull_resistor_5 (.node(IO_adrr[3]));
  Pull_Resistor pull_resistor_6 (.node(cdm_8_mark5_1_p10[4]));
  Pull_Resistor pull_resistor_7 (.node(cdm_8_mark5_1_p10[5]));
  Pull_Resistor pull_resistor_8 (.node(cdm_8_mark5_1_p10[6]));
  Pull_Resistor pull_resistor_9 (.node(cdm_8_mark5_1_p10[7]));

  // Other names for the same wires on the sheet: Rd_wr = in_out

  // Notes on the sheet:
  //   contents of rom_1 (hex, n*v repeats v):
  //   d0 f3 d2 f4 d1 0 a1 8d 5 e5 6 d1 0 fb 8f ab ee 6
endmodule

module walk (
  input  clock,
  input  [31:0] A,
  input  [31:0] B,
  output [31:0] Aout,
  output [31:0] Bout
);

  wire [1:1] not_1_out, not_2_out;

  Pull_Resistor pull_resistor_1 (.node(clock));
  not not_1 (not_1_out[1], A[1]);
  not not_2 (not_2_out[1], B[1]);
  Multiplexer #(.width(32)) multiplexer_1 (
    .in0({B[31:2], not_2_out[1], B[0]}), .in1(B), .out(Bout), .sel(clock));  // open: en
  Multiplexer #(.width(32)) multiplexer_2 (
    .in0(A), .in1({A[31:2], not_1_out[1], A[0]}), .out(Aout), .sel(clock));  // open: en
endmodule

module jump (
  input  clock,
  input  [31:0] in,
  output [31:0] out
);

  wire [0:0] multiplexer_1_out, not_1_out;
  wire [31:0] shifter_1_out;

  not not_1 (not_1_out[0], in[0]);
  Multiplexer #(.width(32)) multiplexer_1 (
    .in0({in[31:1], not_1_out[0]}), .in1(shifter_1_out), .out({out[31:1], multiplexer_1_out[0]}), .sel(clock));  // open: en
  Shifter #(.width(32), .shift("rl")) shifter_1 (.in({in[31:1], not_1_out[0]}), .\dist (5'b00111), .out(shifter_1_out));
  not not_2 (out[0], multiplexer_1_out[0]);
endmodule

module mover (
  input  in_1,
  input  [31:0] in_2,
  output [31:0] out_3,
  output [31:0] out_4,
  output [31:0] out_5,
  output [31:0] out_6,
  output [31:0] out_7,
  output [31:0] out_8,
  output [31:0] out_9,
  output [31:0] out_10,
  output [31:0] out_11,
  output [31:0] out_12,
  output [31:0] out_13,
  output [31:0] out_14,
  output [31:0] out_15,
  output [31:0] out_16,
  output [31:0] out_17,
  output [31:0] out_18,
  output [31:0] out_19,
  output [31:0] out_20,
  output [31:0] out_21,
  output [31:0] out_22,
  output [31:0] out_23,
  output [31:0] out_24,
  output [31:0] out_25,
  output [31:0] out_26,
  output [31:0] out_27,
  output [31:0] out_28,
  output [31:0] out_29,
  output [31:0] out_30,
  output [31:0] out_31,
  output [31:0] out_32,
  output [31:0] out_33,
  output [31:0] out_34
);

  wire comparator_1_eq, not_1_out;
  wire [31:0] multiplexer_1_out;

  Multiplexer #(.width(32)) multiplexer_1 (
    .in0(32'h1), .in1(in_2), .out(multiplexer_1_out), .sel(not_1_out));  // open: en
  not not_1 (not_1_out, comparator_1_eq);
  Comparator #(.width(32)) comparator_1 (.a(in_2), .b({32{1'b0}}), .eq(comparator_1_eq));  // open: gt, lt
  Pull_Resistor #(.pull(1)) pull_resistor_1 (.node(comparator_1_eq));
  Register #(.width(32)) register_1 (.D(multiplexer_1_out), .Q(out_3), .clk(in_1));  // open: en, clr
  Register #(.width(32)) register_2 (.D(out_3), .Q(out_4), .clk(in_1));  // open: en, clr
  Register #(.width(32)) register_3 (.D(out_4), .Q(out_5), .clk(in_1));  // open: en, clr
  Register #(.width(32)) register_4 (.D(out_5), .Q(out_6), .clk(in_1));  // open: en, clr
  Register #(.width(32)) register_5 (.D(out_6), .Q(out_7), .clk(in_1));  // open: en, clr
  Register #(.width(32)) register_6 (.D(out_7), .Q(out_8), .clk(in_1));  // open: en, clr
  Register #(.width(32)) register_7 (.D(out_8), .Q(out_9), .clk(in_1));  // open: en, clr
  Register #(.width(32)) register_8 (.D(out_9), .Q(out_10), .clk(in_1));  // open: en, clr
  Register #(.width(32)) register_9 (.D(out_10), .Q(out_11), .clk(in_1));  // open: en, clr
  Register #(.width(32)) register_10 (.D(out_11), .Q(out_12), .clk(in_1));  // open: en, clr
  Register #(.width(32)) register_11 (.D(out_12), .Q(out_13), .clk(in_1));  // open: en, clr
  Register #(.width(32)) register_12 (.D(out_13), .Q(out_14), .clk(in_1));  // open: en, clr
  Register #(.width(32)) register_13 (.D(out_14), .Q(out_15), .clk(in_1));  // open: en, clr
  Register #(.width(32)) register_14 (.D(out_15), .Q(out_16), .clk(in_1));  // open: en, clr
  Register #(.width(32)) register_15 (.D(out_16), .Q(out_17), .clk(in_1));  // open: en, clr
  Register #(.width(32)) register_16 (.D(out_17), .Q(out_18), .clk(in_1));  // open: en, clr
  Register #(.width(32)) register_17 (.D(out_18), .Q(out_19), .clk(in_1));  // open: en, clr
  Register #(.width(32)) register_18 (.D(out_19), .Q(out_20), .clk(in_1));  // open: en, clr
  Register #(.width(32)) register_19 (.D(out_20), .Q(out_21), .clk(in_1));  // open: en, clr
  Register #(.width(32)) register_20 (.D(out_21), .Q(out_22), .clk(in_1));  // open: en, clr
  Register #(.width(32)) register_21 (.D(out_22), .Q(out_23), .clk(in_1));  // open: en, clr
  Register #(.width(32)) register_22 (.D(out_23), .Q(out_24), .clk(in_1));  // open: en, clr
  Register #(.width(32)) register_23 (.D(out_24), .Q(out_25), .clk(in_1));  // open: en, clr
  Register #(.width(32)) register_24 (.D(out_25), .Q(out_26), .clk(in_1));  // open: en, clr
  Register #(.width(32)) register_25 (.D(out_26), .Q(out_27), .clk(in_1));  // open: en, clr
  Register #(.width(32)) register_26 (.D(out_27), .Q(out_28), .clk(in_1));  // open: en, clr
  Register #(.width(32)) register_27 (.D(out_28), .Q(out_29), .clk(in_1));  // open: en, clr
  Register #(.width(32)) register_28 (.D(out_29), .Q(out_30), .clk(in_1));  // open: en, clr
  Register #(.width(32)) register_29 (.D(out_30), .Q(out_31), .clk(in_1));  // open: en, clr
  Register #(.width(32)) register_30 (.D(out_31), .Q(out_32), .clk(in_1));  // open: en, clr
  Register #(.width(32)) register_31 (.D(out_32), .Q(out_33), .clk(in_1));  // open: en, clr
  Register #(.width(32)) register_32 (.D(out_33), .Q(out_34), .clk(in_1));  // open: en, clr
endmodule

module cactus_generator (
  input  clock,
  output [31:0] out
);

  wire and_1_out, and_2_out, and_3_out, and_4_out, counter_1_carry, counter_2_carry, demultiplexer_1_out0,
       demultiplexer_1_out1, demultiplexer_1_out2, demultiplexer_1_out3, not_1_out, not_2_out, not_3_out,
       not_4_out, not_5_out, s_r_ff_1_q;
  wire [1:0] counter_2_q, random_1_out;
  wire [31:0] controlled_buffer_1_out, controlled_buffer_2_out, controlled_buffer_3_out,
       controlled_buffer_4_out, multiplexer_1_out;

  Counter #(.max('h12), .trigger("falling")) counter_1 (
    .carry(counter_1_carry), .clk(clock));  // open: load, D, count, Q, clr
  assign controlled_buffer_1_out = demultiplexer_1_out0 ? 32'h3d : 32'bz;  // Controlled_Buffer controlled_buffer_1
  assign controlled_buffer_2_out = demultiplexer_1_out0 ? 32'h3d : 32'bz;  // Controlled_Buffer controlled_buffer_2
  assign controlled_buffer_3_out = demultiplexer_1_out0 ? 32'h3d : 32'bz;  // Controlled_Buffer controlled_buffer_3
  assign controlled_buffer_4_out = demultiplexer_1_out0 ? 32'h3d : 32'bz;  // Controlled_Buffer controlled_buffer_4
  S_R_Flip_Flop s_r_ff_1 (.Q(s_r_ff_1_q), .preset(counter_1_carry), .reset(and_1_out));  // open: S, clk, R, Qn, en
  assign controlled_buffer_1_out = demultiplexer_1_out1 ? 32'h401 : 32'bz;  // Controlled_Buffer controlled_buffer_5
  assign controlled_buffer_2_out = demultiplexer_1_out1 ? 32'h201 : 32'bz;  // Controlled_Buffer controlled_buffer_6
  assign controlled_buffer_3_out = demultiplexer_1_out1 ? 32'h301 : 32'bz;  // Controlled_Buffer controlled_buffer_7
  assign controlled_buffer_4_out = demultiplexer_1_out1 ? 32'h401 : 32'bz;  // Controlled_Buffer controlled_buffer_8
  not not_1 (not_1_out, not_3_out);
  and and_1 (and_1_out, not_1_out, not_3_out);
  not not_2 (not_2_out, s_r_ff_1_q);
  assign controlled_buffer_1_out = demultiplexer_1_out2 ? 32'h7 : 32'bz;  // Controlled_Buffer controlled_buffer_9
  assign controlled_buffer_2_out = demultiplexer_1_out2 ? 32'h10000f : 32'bz;  // Controlled_Buffer controlled_buffer_10
  assign controlled_buffer_3_out = demultiplexer_1_out2 ? 32'hf : 32'bz;  // Controlled_Buffer controlled_buffer_11
  assign controlled_buffer_4_out = demultiplexer_1_out2 ? 32'h7 : 32'bz;  // Controlled_Buffer controlled_buffer_12
  and and_2 (and_2_out, clock, s_r_ff_1_q);
  not not_3 (not_3_out, counter_2_carry);
  and and_3 (and_3_out, s_r_ff_1_q, not_2_out);
  assign controlled_buffer_1_out = demultiplexer_1_out3 ? 32'h7 : 32'bz;  // Controlled_Buffer controlled_buffer_13
  assign controlled_buffer_2_out = demultiplexer_1_out3 ? 32'hf : 32'bz;  // Controlled_Buffer controlled_buffer_14
  assign controlled_buffer_3_out = demultiplexer_1_out3 ? 32'h1f : 32'bz;  // Controlled_Buffer controlled_buffer_15
  assign controlled_buffer_4_out = demultiplexer_1_out3 ? 32'h3f : 32'bz;  // Controlled_Buffer controlled_buffer_16
  not not_4 (not_4_out, and_2_out);
  Random #(.width(2)) random_1 (.clk(and_3_out), .out(random_1_out));  // open: next, clr
  and and_4 (and_4_out, not_4_out, not_5_out);
  not not_5 (not_5_out, not_4_out);
  Counter #(.width(2), .max('h3), .trigger("falling")) counter_2 (
    .Q(counter_2_q), .carry(counter_2_carry), .clk(and_4_out));  // open: load, D, count, clr
  Demultiplexer #(.select(2)) demultiplexer_1 (
    .out0(demultiplexer_1_out0), .out1(demultiplexer_1_out1), .out2(demultiplexer_1_out2),
    .out3(demultiplexer_1_out3), .in(1'b1), .sel(random_1_out));  // open: en
  Multiplexer #(.select(2), .width(32)) multiplexer_1 (
    .in0(controlled_buffer_1_out), .in1(controlled_buffer_2_out), .in2(controlled_buffer_3_out),
    .in3(controlled_buffer_4_out), .out(multiplexer_1_out), .sel(counter_2_q));  // open: en
  // Probe on controlled_buffer_1_out
  Multiplexer #(.width(32)) multiplexer_2 (
    .in0({32{1'b0}}), .in1(multiplexer_1_out), .out(out), .sel(s_r_ff_1_q));  // open: en
  // Probe on controlled_buffer_2_out
  // Probe on controlled_buffer_3_out
  // Probe on controlled_buffer_4_out
endmodule

module delayer4 (
  input  [7:0] Data,
  input  Selector,
  input  [3:0] Adress,
  input  In_Out,
  output [7:0] out_5,
  output [7:0] out_6
);

  wire and_1_out, and_2_out, decoder_1_out0, decoder_2_out0;

  Register #(.trigger("falling")) register_1 (.D(Data), .Q(out_5), .clk(decoder_1_out0));  // open: en, clr
  Register #(.trigger("falling")) register_2 (.D(Data), .Q(out_6), .clk(decoder_2_out0));  // open: en, clr
  Decoder #(.disabled(0)) decoder_1 (.out0(decoder_1_out0), .sel(In_Out), .en(and_1_out));  // open: out1
  and and_1 (and_1_out, Selector, Adress[0], Adress[1], ~Adress[2], ~Adress[3]);  // AND_Gate
  and and_2 (and_2_out, Selector, Adress[0], ~Adress[1], Adress[2], Adress[3]);  // AND_Gate
  Decoder #(.disabled(0)) decoder_2 (.out0(decoder_2_out0), .sel(In_Out), .en(and_2_out));  // open: out1
endmodule

module counter (
  input  [7:0] Lower,
  input  [7:0] Upper
);
endmodule

module jumper (
  input  chooser,
  input  Clock,
  input  [31:0] in_3,
  input  [31:0] Selector,
  output [31:0] out_5
);

  wire not_1_out, or_1_out;
  wire [2:0] counter_1_q;
  wire [4:0] multiplexer_1_out;
  wire [31:0] shifter_1_out;

  not not_1 (not_1_out, chooser);
  Counter #(.width(3), .max('h6), .ongoal("stay")) counter_1 (
    .load(not_1_out), .D(3'b001), .Q(counter_1_q), .clk(Clock));  // open: count, carry, clr
  Multiplexer #(.select(3), .width(5), .enable("false")) multiplexer_1 (
    .in0({5{1'b0}}), .in1(5'b00001), .in2(5'b00010), .in3(5'b00011), .in4(5'b00100), .in5(5'b00101),
    .in6(5'b00110), .out(multiplexer_1_out), .sel(counter_1_q));  // open: in7
  or or_1 (or_1_out, counter_1_q[0], counter_1_q[1], counter_1_q[2]);
  D_Flip_Flop #(.trigger("falling")) d_ff_1 (.clk(Clock), .D(or_1_out));  // open: Q, Qn, preset, en, reset
  Shifter #(.width(32)) shifter_1 (.in(in_3), .\dist (multiplexer_1_out), .out(shifter_1_out));
  Adder #(.width(32)) adder_1 (.a(shifter_1_out), .b(Selector), .out(out_5));  // open: cin, cout
endmodule
